// Digital circuit remoteI.dig as structural Verilog
// This circuit allows the connection to 8 byte remote inputs/outputs.
// There are 8 bytes to be connected to remote actuators (O0..O7), and 8 bytes to be connected to remote sensors (I0..i7).
// The connection use a TCP server implemented by the Telnet component at port 12345.
// The bytes exchanged are sent/received at the clock frequency (for instance 1000Hz).
// The sent is done as soon as one of the input bytes change its value.
module remoteI (
  input  ck,
  output I0,
  output I1,
  output I2,
  output I3,
  output I4,
  output I5,
  output I6,
  output I7
);

  wire telnet_1_av;
  wire [7:0] notconnected_1_out, telnet_1_out;

  // NotConnected on notconnected_1_out
  Telnet #(.telnetEscape("false"), .port(13370)) telnet_1 (
    .in(notconnected_1_out), .C(ck), .wr(1'b0), .rd(telnet_1_av), .out(telnet_1_out), .av(telnet_1_av));
  Register #(.Bits(8)) register_1 (.D(telnet_1_out), .C(ck), .en(telnet_1_av), .Q({I7, I6, I5, I4, I3, I2, I1, I0}));

  // Notes on the sheet:
  //   ck: Hz: 100
endmodule
