// Digital circuit remoteO.dig as structural Verilog
// This circuit allows the connection to 8 byte remote inputs/outputs.
// There are 8 bytes to be connected to remote actuators (O0..O7), and 8 bytes to be connected to remote sensors (I0..i7).
// The connection use a TCP server implemented by the Telnet component at port 12345.
// The bytes exchanged are sent/received at the clock frequency (for instance 1000Hz).
// The sent is done as soon as one of the input bytes change its value.
module remoteO (
  input  O0,
  input  O1,
  input  O2,
  input  O3,
  input  O4,
  input  O5,
  input  O6,
  input  O7,
  input  ck
);

  wire comparator_1_eq, d_ff_1_q, not_1_out, or_1_out, reset_1_out, rs_ff_as_1_q;
  wire [7:0] register_1_q, register_2_q;

  Register #(.Bits(8)) register_1 (.D({O7, O6, O5, O4, O3, O2, O1, O0}), .C(ck), .en(1'b1), .Q(register_1_q));
  Register #(.Bits(8)) register_2 (.D(register_1_q), .C(ck), .en(1'b1), .Q(register_2_q));
  Reset #(.invertOutput("false")) reset_1 (.out(reset_1_out));
  Comparator #(.Bits(8)) comparator_1 (.a(register_1_q), .b(register_2_q), .eq(comparator_1_eq));  // open: gt, lt
  RS_FF_AS rs_ff_as_1 (.S(reset_1_out), .R(d_ff_1_q), .Q(rs_ff_as_1_q));  // open: nQ
  not not_1 (not_1_out, comparator_1_eq);
  D_FF d_ff_1 (.D(rs_ff_as_1_q), .C(ck), .Q(d_ff_1_q));  // open: nQ
  or or_1 (or_1_out, not_1_out, d_ff_1_q);
  Telnet #(.telnetEscape("false"), .port(13371)) telnet_1 (
    .in(register_1_q), .C(ck), .wr(or_1_out), .rd(1'b0));  // open: out, av

  // Notes on the sheet:
  //   O2: default 50
  //   O3: default 50
  //   O4: default 50
  //   O5: default 50
  //   O6: default 50
  //   O7: default 50
  //   ck: Hz: 100
endmodule
