// Digital circuit testIO.dig as structural Verilog
module testIO (
  input  _1kHz,
  input  L2Y,
  input  L3R,
  input  L1G
);

  wire and_1_out, not_1_out, not_2_out, or_1_out, remotei_1_p2, remotei_1_p3;

  // remoteI remotei_1: pin names not known; wires that end beside it: _1kHz, remotei_1_p2, remotei_1_p3
  not not_1 (not_1_out, remotei_1_p2);
  not not_2 (not_2_out, remotei_1_p3);
  LED B1 (.in(not_1_out));
  LED B2 (.in(not_2_out));
  and and_1 (and_1_out, not_2_out, not_1_out);
  or or_1 (or_1_out, and_1_out, L3R);
  remoteO remoteo_1 (
    .O0(L1G), .O1(L2Y), .O2(or_1_out), .O3(1'b0), .O4(1'b0), .O5(1'b0), .O6(1'b0), .O7(1'b0), .ck(_1kHz));

  // Notes on the sheet:
  //   _1kHz: Hz: 1000
endmodule
